// Logisim project VrajPatelLab03.circ as structural Verilog: 9 circuits, main circuit  Main ALU Circuit
module _16_Bit_AND (
  input  [15:0] A,
  input  [15:0] B,
  output [15:0] OUT
);

  assign OUT = A & B;  // AND_Gate AND, 16 bits wide

  // Notes on the sheet:
  //   16-Bit AND
endmodule

module _16_Bit_OR (
  input  [15:0] A,
  input  [15:0] B,
  output [15:0] OUT
);

  assign OUT = A | B;  // OR_Gate or_1, 16 bits wide

  // Notes on the sheet:
  //   16-Bit OR
endmodule

module _16_Bit_XOR (
  input  [15:0] A,
  input  [15:0] B,
  output [15:0] OUT
);

  assign OUT = A ^ B;  // XOR_Gate xor_1, 16 bits wide

  // Notes on the sheet:
  //   16-bit XOR
endmodule

module _16_Bit_Inverter (
  input  [15:0] A,
  output [15:0] OUT
);

  assign OUT = ~A;  // NOT_Gate not_1, 16 bits wide

  // Notes on the sheet:
  //   16-Bit Inverter
endmodule

module _16_Bit_Adder (
  input  [15:0] A,
  input  [15:0] B,
  output [15:0] SUM,
  output C_add
);

  wire adder_1_cout;

  Adder #(.width(16)) adder_1 (.a(A), .b(B), .out(SUM), .cin(1'b0), .cout(adder_1_cout));

  // Notes on the sheet:
  //   16-Bit Adder
  //   Please notice that you need to generate the four flag bits for the adder.
endmodule

module _16_Bit_Subtractor (
  input  [15:0] A,
  input  [15:0] B,
  output [15:0] OUT,
  output C_Sub
);

  wire subtractor_1_bout;

  Subtractor #(.width(16)) subtractor_1 (.a(A), .b(B), .out(OUT), .bin(1'b0), .bout(subtractor_1_bout));

  // Notes on the sheet:
  //   16-Bit Subtractor
  //   Please notice that you need to generate the four flag bits for the subtractor
endmodule

module _16_Bit_Left_Shifter_Circuit (
  input  [15:0] A,
  input  [3:0] B,
  output [15:0] OUT
);

  Shifter #(.width(16)) shifter_1 (.in(A), .\dist (B), .out(OUT));

  // Notes on the sheet:
  //   16-Bit Left Shifter Circuit
  //   Shift A to left by B bits
endmodule

module _16_Bit_Right_Shfit_Circuit (
  input  [15:0] A,
  input  [3:0] B,
  output [15:0] OUT
);

  Shifter #(.width(16), .shift("lr")) shifter_1 (.in(A), .\dist (B), .out(OUT));

  // Notes on the sheet:
  //   16-Bit Right Shifter Circuit
  //   Shift A to Right by B bits
endmodule

module Main_ALU_Circuit (
  input  [15:0] A,
  input  [15:0] B,
  input  [2:0] S,
  input  S0,
  input  [3:0] Shift_Bits,
  input  [15:0] in_6,
  output [15:0] ALU_OUTPUT,
  output Negative,
  output Carry,
  output Zero,
  output Overflow
);

  wire and_1_out, and_2_out, n16_bit_adder_1_c_add, n16_bit_subtractor_1_c_sub, not_1_out, not_2_out,
       not_3_out, xor_1_out;
  wire [15:0] n16_bit_adder_1_sum, n16_bit_and_1_out, n16_bit_inverter_1_out,
       n16_bit_left_shifter_circuit_1_out, n16_bit_or_1_out, n16_bit_right_shfit_circuit_1_out,
       n16_bit_subtractor_1_out, n16_bit_xor_1_out;

  _16_Bit_Adder u_16_bit_adder_1 (.A(A), .B(B), .SUM(n16_bit_adder_1_sum), .C_add(n16_bit_adder_1_c_add));
  _16_Bit_Subtractor u_16_bit_subtractor_1 (
    .A(A), .B(B), .OUT(n16_bit_subtractor_1_out), .C_Sub(n16_bit_subtractor_1_c_sub));
  _16_Bit_AND u_16_bit_and_1 (.A(A), .B(B), .OUT(n16_bit_and_1_out));
  _16_Bit_OR u_16_bit_or_1 (.A(A), .B(B), .OUT(n16_bit_or_1_out));
  _16_Bit_XOR u_16_bit_xor_1 (.A(A), .B(B), .OUT(n16_bit_xor_1_out));
  _16_Bit_Inverter u_16_bit_inverter_1 (.A(A), .OUT(n16_bit_inverter_1_out));
  _16_Bit_Right_Shfit_Circuit u_16_bit_right_shfit_circuit_1 (
    .A(A), .B(Shift_Bits), .OUT(n16_bit_right_shfit_circuit_1_out));
  _16_Bit_Left_Shifter_Circuit u_16_bit_left_shifter_circuit_1 (
    .A(A), .B(Shift_Bits), .OUT(n16_bit_left_shifter_circuit_1_out));
  Multiplexer #(.select(3), .width(16)) multiplexer_1 (
    .in0(n16_bit_adder_1_sum), .in1(n16_bit_subtractor_1_out), .in2(n16_bit_and_1_out),
    .in3(n16_bit_or_1_out), .in4(n16_bit_xor_1_out), .in5(n16_bit_inverter_1_out),
    .in6(n16_bit_right_shfit_circuit_1_out), .in7(n16_bit_left_shifter_circuit_1_out), .out(ALU_OUTPUT),
    .sel(S));  // open: en
  Comparator #(.width(16)) comparator_1 (.a(ALU_OUTPUT), .b(in_6), .eq(Zero));  // open: gt, lt
  xor xor_1 (xor_1_out, B[15], S0);
  Multiplexer multiplexer_2 (
    .in0(n16_bit_adder_1_c_add), .in1(n16_bit_subtractor_1_c_sub), .out(Carry), .sel(S0));  // open: en
  not not_1 (not_1_out, ALU_OUTPUT[15]);
  not not_2 (not_2_out, xor_1_out);
  not not_3 (not_3_out, A[15]);
  and and_1 (and_1_out, not_2_out, ALU_OUTPUT[15], not_3_out);
  and and_2 (and_2_out, not_1_out, xor_1_out, A[15]);
  or or_1 (Overflow, and_2_out, and_1_out);

  assign Negative = ALU_OUTPUT[15];

  // Notes on the sheet:
  //   Main ALU Circuit to Build
  //   Needs to use all the subcircuits you built
endmodule
